// Logisim project project_1.circ as structural Verilog
module cXOR (
  input  a,
  input  b,
  output y
);

  wire and_1_out, and_2_out, not_1_out, not_2_out;

  not not_1 (not_1_out, a);
  not not_2 (not_2_out, b);
  and and_1 (and_1_out, not_1_out, b);
  and and_2 (and_2_out, a, not_2_out);
  or or_1 (y, and_1_out, and_2_out);
endmodule

module cNOT (
  input  a,
  output y
);

  nand nand_1 (y, a, a);
endmodule

module cAND (
  input  a,
  input  b,
  output y
);

  wire nand_1_out;

  nand nand_1 (nand_1_out, a, b);
  cNOT cnot_1 (.a(nand_1_out), .y(y));
endmodule

module cOR (
  input  a,
  input  b,
  output y
);

  wire nand_1_out, nand_2_out;

  nand nand_1 (nand_1_out, a, a);
  nand nand_2 (nand_2_out, b, b);
  nand nand_3 (y, nand_1_out, nand_2_out);
endmodule

module cMUX (
  input  a,
  input  s,
  input  b,
  output y
);

  wire and_1_out, and_2_out, not_1_out;

  not not_1 (not_1_out, s);
  and and_1 (and_1_out, a, not_1_out);
  and and_2 (and_2_out, s, b);
  or or_1 (y, and_1_out, and_2_out);
endmodule

module cDMUX (
  input  i,
  input  s,
  output a,
  output b
);

  wire not_1_out;

  not not_1 (not_1_out, s);
  and and_1 (a, i, not_1_out);
  and and_2 (b, i, s);
endmodule

module c2NOT (
  input  [1:0] i,
  output [1:0] o
);

  cNOT cnot_1 (.a(i[0]), .y(o[0]));
  cNOT cnot_2 (.a(i[1]), .y(o[1]));
endmodule

module cOR8Way (
  input  [7:0] i,
  output o
);

  wire or_1_out, or_2_out;

  or or_1 (or_1_out, i[0], i[1], i[2], i[3]);
  or or_2 (or_2_out, i[4], i[5], i[6], i[7]);
  or or_3 (o, or_1_out, or_2_out);
endmodule
