// Logisim project project_2.circ as structural Verilog: 7 circuits, main circuit adder_half
module main (
);

  adder_16b adder_16b_1 ();  // open: c, a, b, sum, car
endmodule

module adder_half (
  input  a,
  input  b,
  output sum,
  output car
);

  xor xor_1 (sum, a, b);
  and and_1 (car, a, b);
endmodule

module adder_full (
  input  a,
  input  b,
  input  c,
  output sum,
  output car
);

  wire adder_half_1_car, adder_half_1_sum, adder_half_2_car;

  adder_half adder_half_1 (.a(a), .b(b), .sum(adder_half_1_sum), .car(adder_half_1_car));
  adder_half adder_half_2 (.a(adder_half_1_sum), .b(c), .sum(sum), .car(adder_half_2_car));
  or or_1 (car, adder_half_2_car, adder_half_1_car);
endmodule

module adder_4b (
  input  c,
  input  [3:0] a,
  input  [3:0] b,
  output [3:0] sum,
  output car
);

  wire adder_full_1_car, adder_full_2_car, adder_full_3_car;

  adder_full adder_full_1 (.a(a[0]), .b(b[0]), .c(c), .sum(sum[0]), .car(adder_full_1_car));
  adder_full adder_full_2 (.a(a[1]), .b(b[1]), .c(adder_full_1_car), .sum(sum[1]), .car(adder_full_2_car));
  adder_full adder_full_3 (.a(a[2]), .b(b[2]), .c(adder_full_2_car), .sum(sum[2]), .car(adder_full_3_car));
  adder_full adder_full_4 (.a(a[3]), .b(b[3]), .c(adder_full_3_car), .sum(sum[3]), .car(car));

  // Other names for the same wires on the sheet: a1 = a[0]; a2 = a[1]; a3 = a[2]; a4 = a[3]; b1 = b[0]; b2 = b[1];
  //   b3 = b[2]; b4 = b[3]; oc = car; o1 = sum[0]; o2 = sum[1]; o3 = sum[2]; o4 = sum[3]
endmodule

module adder_8b (
  input  c,
  input  [7:0] a,
  input  [7:0] b,
  output [7:0] sum,
  output car
);

  wire adder_4b_1_car;

  adder_4b adder_4b_1 (.a(a[3:0]), .b(b[3:0]), .c(c), .car(adder_4b_1_car), .sum(sum[3:0]));
  adder_4b adder_4b_2 (.a(a[7:4]), .b(b[7:4]), .c(adder_4b_1_car), .car(car), .sum(sum[7:4]));

  // Other names for the same wires on the sheet: a1[3:0] = a[3:0]; a2[3:0] = a[7:4]; b1[3:0] = b[3:0];
  //   b2[3:0] = b[7:4]
endmodule

module adder_16b (
  input  c,
  input  [15:0] a,
  input  [15:0] b,
  output [15:0] sum,
  output car
);

  wire adder_8b_1_car;

  adder_8b adder_8b_1 (.a(a[7:0]), .b(b[7:0]), .c(c), .sum(sum[7:0]), .car(adder_8b_1_car));
  adder_8b adder_8b_2 (.a(a[15:8]), .b(b[15:8]), .c(adder_8b_1_car), .sum(sum[15:8]), .car(car));

  // Other names for the same wires on the sheet: a1[7:0] = a[7:0]; a2[7:0] = a[15:8]; b1[7:0] = b[7:0];
  //   b2[7:0] = b[15:8]
endmodule

module alu (
  input  [15:0] x,
  input  zx,
  input  f,
  input  nx,
  input  no,
  input  [15:0] y,
  input  zy,
  input  ny,
  output [15:0] val
);

  wire not_3_out;
  wire [15:0] adder_1_out, and_1_out, demultiplexer_1_out0, demultiplexer_1_out1, demultiplexer_2_out0,
       demultiplexer_2_out1, demultiplexer_3_out0, demultiplexer_3_out1, demultiplexer_4_out0,
       demultiplexer_4_out1, demultiplexer_5_out0, demultiplexer_5_out1, multiplexer_1_out,
       multiplexer_2_out, multiplexer_3_out, multiplexer_4_out, multiplexer_5_out, not_1_out, not_2_out,
       not_4_out;

  Multiplexer #(.width(16)) multiplexer_1 (.in0(x), .in1({16{1'b0}}), .out(multiplexer_1_out), .sel(zx));
  Demultiplexer #(.width(16)) demultiplexer_1 (
    .out0(demultiplexer_1_out0), .out1(demultiplexer_1_out1), .in(multiplexer_1_out), .sel(nx));
  Multiplexer #(.width(16)) multiplexer_2 (.in0(y), .in1({16{1'b0}}), .out(multiplexer_2_out), .sel(zy));
  Demultiplexer #(.width(16)) demultiplexer_2 (
    .out0(demultiplexer_2_out0), .out1(demultiplexer_2_out1), .in(multiplexer_2_out), .sel(ny));
  assign not_1_out = ~demultiplexer_1_out1;  // NOT_Gate not_1, 16 bits wide
  assign not_2_out = ~demultiplexer_2_out1;  // NOT_Gate not_2, 16 bits wide
  Multiplexer #(.width(16)) multiplexer_3 (
    .in0(demultiplexer_1_out0), .in1(not_1_out), .out(multiplexer_3_out), .sel(nx));
  Demultiplexer #(.width(16)) demultiplexer_3 (
    .out0(demultiplexer_3_out0), .out1(demultiplexer_3_out1), .in(multiplexer_3_out), .sel(f));
  Multiplexer #(.width(16)) multiplexer_4 (
    .in0(demultiplexer_2_out0), .in1(not_2_out), .out(multiplexer_4_out), .sel(ny));
  Demultiplexer #(.width(16)) demultiplexer_4 (
    .out0(demultiplexer_4_out0), .out1(demultiplexer_4_out1), .in(multiplexer_4_out), .sel(f));
  Adder #(.width(16)) adder_1 (
    .a(demultiplexer_3_out1), .b(demultiplexer_4_out1), .out(adder_1_out));  // open: cin, cout
  assign and_1_out = demultiplexer_4_out0 & demultiplexer_3_out0;  // AND_Gate and_1, 16 bits wide
  not not_3 (not_3_out, f);
  Multiplexer #(.width(16)) multiplexer_5 (
    .in0(adder_1_out), .in1(and_1_out), .out(multiplexer_5_out), .sel(not_3_out));
  Demultiplexer #(.width(16)) demultiplexer_5 (
    .out0(demultiplexer_5_out0), .out1(demultiplexer_5_out1), .in(multiplexer_5_out), .sel(no));
  assign not_4_out = ~demultiplexer_5_out1;  // NOT_Gate not_4, 16 bits wide
  Multiplexer #(.width(16)) multiplexer_6 (.in0(demultiplexer_5_out0), .in1(not_4_out), .out(val), .sel(no));
endmodule
