// Logisim project project_5.circ as structural Verilog: 1 circuit, main circuit CPU
module CPU (
  input  [15:0] ins,
  input  [15:0] inM,
  input  reset,
  output [15:0] outM,
  output writeM,
  output [15:0] addressM,
  output [15:0] pc
);

  wire clck, not_1_out, or_1_out;
  wire [15:0] D_Register_q, multiplexer_1_out, multiplexer_2_out;

  or or_1 (or_1_out, not_1_out, ins[5]);
  not not_1 (not_1_out, ins[15]);
  Clock clock_1 (.out(clck));
  Register #(.width(16)) A_Register (.D(multiplexer_1_out), .en(or_1_out), .clk(clck), .Q(addressM));  // open: clr
  Multiplexer #(.width(16)) multiplexer_1 (.in0(outM), .in1(ins), .out(multiplexer_1_out), .sel(not_1_out));
  Register #(.width(16)) D_Register (.D(outM), .en(ins[4]), .clk(clck), .Q(D_Register_q));  // open: clr
  Counter #(.max('hffff), .width(16)) program_counter (
    .D(addressM), .Q(pc), .clk(clck), .clr(reset));  // open: load, count, carry, up
  Multiplexer #(.width(16)) multiplexer_2 (.in0(addressM), .in1(inM), .out(multiplexer_2_out), .sel(ins[11]));
  alu alu_1 (
    .f(ins[7]), .x(D_Register_q), .y(multiplexer_2_out), .zx(ins[11]), .zy(ins[9]), .nx(ins[10]),
    .ny(ins[8]), .no(ins[6]), .val(outM));

  assign writeM = ins[3];

  // Other names for the same wires on the sheet: dM = ins[3]; dD = ins[4]; dA = ins[5]; regSel = ins[11];
  //   opCode = ins[15]
endmodule
